# Fritzing sketch PCB_prototype (saved by Fritzing 1.0.7)
perfboards: 1

parts:
  J2 = female pin header, 8 pins [form="♀ (female)"]
  J3 = female pin header, 8 pins [form="♀ (female)"]
  J4 = female pin header, 8 pins [form="♀ (female)"]
  J5 = female pin header, 8 pins [form="♀ (female)"]
  J6 = female pin header, 8 pins [form="♀ (female)"]
  J7 = female pin header, 8 pins [form="♀ (female)"]
  J8 = female pin header, 8 pins [form="♀ (female)"]
  J1 = female pin header, 8 pins [form="♀ (female)"]
  J9 = female pin header, 4 pins [form="♀ (female)"]
  J10 = female pin header, 2 pins [form="♀ (female)"]  # not connected
  J11 = female pin header, 2 pins [form="♀ (female)"]  # not connected
  J12 = female pin header, 2 pins [form="♀ (female)"]  # not connected
  J13 = female pin header, 2 pins [form="♀ (female)"]  # not connected
  J14 = female pin header, 4 pins [form="♀ (female)"]
  J15 = female pin header, 4 pins [form="♀ (female)"]
  J16 = female pin header, 4 pins [form="♀ (female)"]
  J17 = female pin header, 2 pins [form="♀ (female)"]  # not connected
  J18 = female pin header, 2 pins [form="♀ (female)"]
  C1 = Electrolytic Capacitor [capacitance=1µF voltage=35V package="100 mil [THT, electrolytic]"]  # not connected
  C2 = Electrolytic Capacitor [capacitance=0.1mF voltage=35V package="100 mil [THT, electrolytic]"]  # not connected
  C3 = Electrolytic Capacitor [capacitance=1µF voltage=35V package="100 mil [THT, electrolytic]"]  # not connected
  C4 = Electrolytic Capacitor [capacitance=1µF voltage=35V package="100 mil [THT, electrolytic]"]  # not connected
  Bauteil1 = Arduino Uno (Rev3)
  M5 = RioRand LM2596
  V1 = DC Power Supply [voltage=12V internal_resistance=1Ω max_current=0.1A]
  C5 = Electrolytic Capacitor [capacitance=2.2mF voltage=50V package="100 mil [THT, electrolytic]"]  # not connected

nets:
  N1: J2.pin7, Bauteil1.D10_PWM/SS
  N2: J2.pin8, Bauteil1.D9_PWM
  N3: J3.pin1, M5.Pin_1, V1.Pin_2
  N4: J3.pin3, J9.pin1
  N5: J3.pin4, J9.pin2
  N6: J3.pin5, J9.pin3
  N7: J3.pin6, J9.pin4
  N8: J4.pin3, J14.pin1
  N9: J4.pin4, J14.pin2
  N10: J4.pin5, J14.pin3
  N11: J4.pin6, J14.pin4
  N12: J4.pin7, Bauteil1.VIN, M5.Pin_3
  N13: J4.pin8, J1.pin1, J18.pin1
  N14: J5.pin1, Bauteil1.D4
  N15: J5.pin2, Bauteil1.D5_PWM
  N16: J6.pin1, Bauteil1.D7
  N17: J6.pin2, Bauteil1.D6_PWM
  N18: J6.pin8, J7.pin1
  N19: J7.pin3, J15.pin1
  N20: J7.pin4, J15.pin2
  N21: J7.pin5, J15.pin3
  N22: J7.pin6, J15.pin4
  N23: J8.pin3, J16.pin1
  N24: J8.pin4, J16.pin2
  N25: J8.pin5, J16.pin3
  N26: J8.pin6, J16.pin4
  N27: J1.pin7, Bauteil1.D11_PWM/MOSI
  N28: J1.pin8, Bauteil1.D12/MISO
  N29: Bauteil1.GND, M5.Pin_4
  N30: M5.Pin_2, V1.Pin_1

notes:
  EN VM
  MS1 GND
  MS2 M2B
  SPREAD M2A
  UART M1A
  UART M1B
  STEP VIO
  DIR GND
  GND DIR
  VIO STEP
  M1B UART
  M1A UART
  M2A SPREAD
  M2B MS2
  GND MS1
  VM EN
